# Fritzing sketch Esp8266Sim808 (saved by Fritzing 0.9.3b)
circuit board: 7.39662cm x 5.69345cm
perfboards: 1

parts:
  V1 = DC Power [voltage=12V]
  C4 = Ceramic Capacitor [capacitance=100nF voltage=16V package="100 mil [THT, multilayer]"]
  C3 = Ceramic Capacitor [capacitance=100nF voltage=16V package="100 mil [THT, multilayer]"]
  BME280 = BME280 Breakout
  R1 = Resistor [tolerance=±5% resistance=680k package=THT]
  WeMos_D1_Mini1_lite = WeMos D1 Mini
  R2 = Resistor [tolerance=±5% resistance=100k package=THT]
  C2 = Electrolytic Capacitor [capacitance=1µF voltage=16V package="100 mil [THT, electrolytic]"]
  C1 = Electrolytic Capacitor [capacitance=1µF voltage=16V package="100 mil [THT, electrolytic]"]
  U2 = MCP1703 Voltage Regulator [part_number=SOT-89 package="TO92 [THT]"]

nets:
  N1: V1.V+, R1.Pin_1
  N2: V1.V-, C3.0, R2.Pin_0
  N3: C4.0, WeMos_D1_Mini1_lite.G, C2.-, C1.-
  3.3V: C4.1, BME280.3.3V, WeMos_D1_Mini1_lite.3V3
  N4: C3.1, R1.Pin_0, WeMos_D1_Mini1_lite.A0, R2.Pin_1
  N5: BME280.GND, WeMos_D1_Mini1_lite.D4
  N6: BME280.SDI/SDA, WeMos_D1_Mini1_lite.D2
  N7: BME280.SCK/SCL, WeMos_D1_Mini1_lite.D1
  N8: WeMos_D1_Mini1_lite.D0, WeMos_D1_Mini1_lite.RST
  N9: C2.+, U2.Vin

custom parts:
  MCP1703 Voltage Regulator: A MCP1703 Low Dropout Fixed Voltage Regulator (available in 1.2V, 1.5V, 1.8V, 2.5V, 2.8V, 3.0V, 3.3V, 4.0V, 5.0V)
